# Fritzing sketch main (saved by Fritzing 0.9.6b)
breadboards: 1

parts:
  PIC_16F877A1 = PIC 16F877A [package=THT]
  LED1 = LED - 5mm [color="Red (633nm)" current=0.030 package="5 mm [THT]"]
  R1 = Resistor [tolerance=±5% power=0.25 resistance=220 package=THT]

nets:
  N1: PIC_16F877A1.VSS#30, R1.Pin_1
  N2: PIC_16F877A1.RB0/INT, LED1.anode
  N3: LED1.cathode, R1.Pin_0
